# Fritzing sketch iot-device-schema (saved by Fritzing 0.9.5d)

parts:
  Raspberry_Pi_2 = Raspberry Pi 3 [part_number=RPI-3-V1.2]
  Part1 = LCD1602-I2C
  A1 = BBAA100043
  S2 = Round Pushbutton
  S3 = Round Pushbutton
  S4 = Round Pushbutton
  Mod1 = KY-012 Active Buzzer Module [package="Breakout board"]

nets:
  N1: Raspberry_Pi_2.GPIO2, Part1.SDA
  N2: Raspberry_Pi_2.GPIO3, Part1.SCL
  GND: Raspberry_Pi_2.GND, Raspberry_Pi_2.GIPO16, Part1.GND, A1.pin4, S2.leg0, S2.leg1, S3.leg1, S4.leg1, Mod1.-
  N3: Raspberry_Pi_2.GIPO21, S3.leg0
  N4: Raspberry_Pi_2.GIPO20, S4.leg0
  N5: Raspberry_Pi_2.GIPO7, A1.pin3
  N6: Raspberry_Pi_2.GIPO8, A1.pin2
  N7: Raspberry_Pi_2.GIPO25, A1.pin1
  N8: Raspberry_Pi_2.GIPO18, Mod1.NC
  5V: Raspberry_Pi_2.5V, Part1.VCC, Mod1.S

custom parts:
  LCD1602-I2C: A standard character display, usually with 2x16 characters. Comes in many colors with LCM1602 IIC attached.
  BBAA100043: BBAA100043 traffic light module.
  KY-012 Active Buzzer Module: Active Piezoelectric Buzzer Module KY-012, it produces single-tone sound when signal is high. (Special thanks to vanepp for fixing the PCB holes and other errors)
